// Logisim project cpu_16b.circ as structural Verilog: 10 circuits, main circuit main
module main (
);

  wire addr_sel, address_decoder_1_bank, address_decoder_1_io, address_decoder_1_memory,
       address_decoder_1_stack, alu_1_lt, alu_1_lt_u, alu_1_zero, alu_a_sel, alu_b_sel, clock_1_out,
       inst_clk, mem_clk, pc_alu_sel, pc_clk, pc_sel, rd_clk;
  wire [1:0] rd_sel;
  wire [2:0] address_decoder_1_mem_sel;
  wire [3:0] rd, rs1, rs2;
  wire [7:0] INST_q;
  wire [15:0] adder_1_out, alu_1_q, imm_dec_1_imm, microcode_1_q, multiplexer_1_out, multiplexer_2_out,
       multiplexer_3_out, multiplexer_4_out, multiplexer_5_out, multiplexer_6_out, multiplexer_7_out, PC_q,
       Regs_q0;

  // Probe on rd_sel
  // Probe on multiplexer_1_out
  Multiplexer #(.select(2), .width(16)) multiplexer_1 (
    .in0(multiplexer_5_out), .in2(alu_1_q), .in3(adder_1_out), .out(multiplexer_1_out), .sel(rd_sel));  // open: in1
  // Probe on multiplexer_5_out
  // Probe on multiplexer_3_out
  // Probe on adder_1_out
  Register #(.width(16)) PC (.D(multiplexer_2_out), .en(1'b1), .clk(pc_clk), .Q(PC_q));  // open: clr
  // Probe on multiplexer_2_out
  Multiplexer #(.width(16)) multiplexer_2 (.in0(adder_1_out), .in1(alu_1_q), .out(multiplexer_2_out), .sel(pc_sel));
  Register #(.width(16)) INST (.D(multiplexer_5_out), .en(1'b1), .clk(inst_clk), .Q({rs2, rs1, INST_q}));  // open: clr
  Multiplexer #(.width(16)) multiplexer_3 (.in0(alu_1_q), .in1(PC_q), .out(multiplexer_3_out), .sel(addr_sel));
  // Probe on multiplexer_4_out
  Multiplexer #(.width(16)) multiplexer_4 (.in0(16'h2), .in1(imm_dec_1_imm), .out(multiplexer_4_out), .sel(pc_alu_sel));
  Adder #(.width(16)) adder_1 (.a(multiplexer_4_out), .b(PC_q), .out(adder_1_out));  // open: cin, cout
  // Probe on PC_q
  address_decoder address_decoder_1 (
    .addr(multiplexer_3_out), .memory(address_decoder_1_memory), .io(address_decoder_1_io),
    .bank(address_decoder_1_bank), .stack(address_decoder_1_stack), .mem_sel(address_decoder_1_mem_sel));  // open: microcode
  microcode microcode_1 (.addr(multiplexer_3_out), .Q(microcode_1_q));  // open: byte
  Multiplexer #(.select(3), .width(16)) multiplexer_5 (
    .in0(microcode_1_q), .out(multiplexer_5_out), .sel(address_decoder_1_mem_sel));  // open: in1, in2, in3, in4, in5, in6, in7
  registers Regs (
    .D(multiplexer_1_out), .RD(rd), .RS1(rs1), .RS2(rs2), .clk(rd_clk), .Q0(Regs_q0), .Q1(multiplexer_5_out));
  // Probe on imm_dec_1_imm
  imm_dec imm_dec_1 (.inst({rs2, rs1, INST_q}), .imm(imm_dec_1_imm));
  Multiplexer #(.width(16)) multiplexer_6 (.in0(PC_q), .in1(Regs_q0), .out(multiplexer_6_out), .sel(alu_a_sel));
  // Probe on multiplexer_6_out
  Multiplexer #(.width(16)) multiplexer_7 (
    .in0(multiplexer_5_out), .in1(imm_dec_1_imm), .out(multiplexer_7_out), .sel(alu_b_sel));
  // Probe on multiplexer_7_out
  Clock clock_1 (.out(clock_1_out));
  control control_1 (
    .zero(alu_1_zero), .lt(alu_1_lt), .lt_u(alu_1_lt_u), .inst({rs2, rs1, INST_q}), .clk(clock_1_out),
    .addr_sel(addr_sel), .rd_sel(rd_sel), .alu_a_sel(alu_a_sel), .alu_b_sel(alu_b_sel), .pc_sel(pc_sel),
    .pc_alu_sel(pc_alu_sel), .mem_clk(mem_clk), .pc_clk(pc_clk), .inst_clk(inst_clk), .rd_clk(rd_clk), .rd(rd));
  alu alu_1 (
    .D0(multiplexer_6_out), .D1(multiplexer_7_out), .alu_sel(INST_q[7:4]), .zero(alu_1_zero), .Q(alu_1_q),
    .lt(alu_1_lt), .lt_u(alu_1_lt_u));
  // Probe on alu_1_q
endmodule

module registers (
  input  [15:0] D,
  input  [3:0] RD,
  input  [3:0] RS1,
  input  [3:0] RS2,
  input  clk,
  output [15:0] Q0,
  output [15:0] Q1
);

  wire demultiplexer_1_out1, demultiplexer_1_out2, demultiplexer_1_out3, demultiplexer_1_out4,
       demultiplexer_1_out5, demultiplexer_1_out6, demultiplexer_1_out7, demultiplexer_1_out8,
       demultiplexer_1_out9, demultiplexer_1_out10, demultiplexer_1_out11, demultiplexer_1_out12,
       demultiplexer_1_out13, demultiplexer_1_out14, demultiplexer_1_out15;
  wire [15:0] register_1_q, register_2_q, register_3_q, register_4_q, register_5_q, register_6_q,
       register_7_q, register_8_q, register_9_q, register_10_q, register_11_q, register_12_q, register_13_q,
       register_14_q, register_15_q;

  Demultiplexer #(.select(4)) demultiplexer_1 (
    .out1(demultiplexer_1_out1), .out2(demultiplexer_1_out2), .out3(demultiplexer_1_out3),
    .out4(demultiplexer_1_out4), .out5(demultiplexer_1_out5), .out6(demultiplexer_1_out6),
    .out7(demultiplexer_1_out7), .out8(demultiplexer_1_out8), .out9(demultiplexer_1_out9),
    .out10(demultiplexer_1_out10), .out11(demultiplexer_1_out11), .out12(demultiplexer_1_out12),
    .out13(demultiplexer_1_out13), .out14(demultiplexer_1_out14), .out15(demultiplexer_1_out15), .in(1'b1),
    .sel(RD));  // open: out0
  Register #(.width(16)) register_1 (.D(D), .en(demultiplexer_1_out1), .clk(clk), .Q(register_1_q));  // open: clr
  Register #(.width(16)) register_2 (.D(D), .en(demultiplexer_1_out2), .clk(clk), .Q(register_2_q));  // open: clr
  Register #(.width(16)) register_3 (.D(D), .en(demultiplexer_1_out3), .clk(clk), .Q(register_3_q));  // open: clr
  Register #(.width(16)) register_4 (.D(D), .en(demultiplexer_1_out4), .clk(clk), .Q(register_4_q));  // open: clr
  Register #(.width(16)) register_5 (.D(D), .en(demultiplexer_1_out5), .clk(clk), .Q(register_5_q));  // open: clr
  Register #(.width(16)) register_6 (.D(D), .en(demultiplexer_1_out6), .clk(clk), .Q(register_6_q));  // open: clr
  Register #(.width(16)) register_7 (.D(D), .en(demultiplexer_1_out7), .clk(clk), .Q(register_7_q));  // open: clr
  Register #(.width(16)) register_8 (.D(D), .en(demultiplexer_1_out8), .clk(clk), .Q(register_8_q));  // open: clr
  Register #(.width(16)) register_9 (.D(D), .en(demultiplexer_1_out9), .clk(clk), .Q(register_9_q));  // open: clr
  Register #(.width(16)) register_10 (.D(D), .en(demultiplexer_1_out10), .clk(clk), .Q(register_10_q));  // open: clr
  Register #(.width(16)) register_11 (.D(D), .en(demultiplexer_1_out11), .clk(clk), .Q(register_11_q));  // open: clr
  Register #(.width(16)) register_12 (.D(D), .en(demultiplexer_1_out12), .clk(clk), .Q(register_12_q));  // open: clr
  Register #(.width(16)) register_13 (.D(D), .en(demultiplexer_1_out13), .clk(clk), .Q(register_13_q));  // open: clr
  Register #(.width(16)) register_14 (.D(D), .en(demultiplexer_1_out14), .clk(clk), .Q(register_14_q));  // open: clr
  Register #(.width(16)) register_15 (.D(D), .en(demultiplexer_1_out15), .clk(clk), .Q(register_15_q));  // open: clr
  Multiplexer #(.select(4), .width(16)) multiplexer_1 (
    .in0({16{1'b0}}), .in1(register_1_q), .in2(register_2_q), .in3(register_3_q), .in4(register_4_q),
    .in5(register_5_q), .in6(register_6_q), .in7(register_7_q), .in8(register_8_q), .in9(register_9_q),
    .in10(register_10_q), .in11(register_11_q), .in12(register_12_q), .in13(register_13_q),
    .in14(register_14_q), .in15(register_15_q), .out(Q0), .sel(RS1));
  Multiplexer #(.select(4), .width(16)) multiplexer_2 (
    .in0({16{1'b0}}), .in1(register_1_q), .in2(register_2_q), .in3(register_3_q), .in4(register_4_q),
    .in5(register_5_q), .in6(register_6_q), .in7(register_7_q), .in8(register_8_q), .in9(register_9_q),
    .in10(register_10_q), .in11(register_11_q), .in12(register_12_q), .in13(register_13_q),
    .in14(register_14_q), .in15(register_15_q), .out(Q1), .sel(RS2));
endmodule

module alu (
  input  [15:0] D0,
  input  [15:0] D1,
  input  [3:0] alu_sel,
  output zero,
  output [15:0] Q,
  output lt,
  output lt_u
);

  wire [15:0] adder_1_out, and_1_out, divider_1_out, divider_1_rem, multiplier_1_out, not_1_out, or_1_out,
       shifter_1_out, shifter_2_out, subtractor_1_out, xor_1_out;

  Adder #(.width(16)) adder_1 (.a(D0), .b(D1), .out(adder_1_out));  // open: cin, cout
  Subtractor #(.width(16)) subtractor_1 (.a(D0), .b(D1), .out(subtractor_1_out));  // open: bin, bout
  Multiplier #(.width(16)) multiplier_1 (.a(D0), .b(D1), .out(multiplier_1_out));  // open: cin, cout
  Divider #(.width(16)) divider_1 (.a(D0), .b(D1), .out(divider_1_out), .rem(divider_1_rem));  // open: upper
  assign and_1_out = D0 & D1;  // AND_Gate and_1, 16 bits wide
  assign or_1_out = D0 | D1;  // OR_Gate or_1, 16 bits wide
  assign xor_1_out = D0 ^ D1;  // XOR_Gate xor_1, 16 bits wide
  assign not_1_out = ~D0;  // NOT_Gate not_1, 16 bits wide
  Shifter #(.width(16)) shifter_1 (.in(D0), .\dist (D1[3:0]), .out(shifter_1_out));
  Shifter #(.shift("lr"), .width(16)) shifter_2 (.in(D0), .\dist (D1[3:0]), .out(shifter_2_out));
  Comparator #(.width(16)) comparator_1 (.a(D0), .b(D1), .lt(lt));  // open: gt, eq
  Comparator #(.mode("unsigned"), .width(16)) comparator_2 (.a(D0), .b(D1), .lt(lt_u));  // open: gt, eq
  Multiplexer #(.select(4), .width(16)) multiplexer_1 (
    .in0(adder_1_out), .in1(subtractor_1_out), .in2(multiplier_1_out), .in3(divider_1_out),
    .in4(divider_1_rem), .in5(and_1_out), .in6(or_1_out), .in7(xor_1_out), .in8(not_1_out),
    .in9(shifter_1_out), .in10(shifter_2_out), .in15(D0), .out(Q), .sel(alu_sel));  // open: in11, in12, in13, in14
  nor nor_1 (zero, Q[0], Q[1], Q[2], Q[3], Q[4], Q[5], Q[6], Q[7], Q[8], Q[9], Q[10], Q[11], Q[12], Q[13], Q[14], Q[15]);
endmodule

module control (
  input  zero,
  input  lt,
  input  lt_u,
  input  [15:0] inst,
  input  clk,
  output addr_sel,
  output [1:0] rd_sel,
  output alu_a_sel,
  output alu_b_sel,
  output pc_sel,
  output pc_alu_sel,
  output mem_clk,
  output pc_clk,
  output inst_clk,
  output rd_clk,
  output [3:0] rd
);

  wire d_ff_1_qn, multiplexer_1_out, multiplexer_8_out, multiplexer_10_out, push, stack;

  D_Flip_Flop d_ff_1 (.D(d_ff_1_qn), .clk(clk), .Q(pc_clk), .Qn(d_ff_1_qn));  // open: preset, reset
  not not_1 (inst_clk, pc_clk);
  and and_1 (push, stack, inst[12]);
  Multiplexer #(.select(4)) multiplexer_1 (
    .in0(1'b0), .in1(1'b0), .in2(1'b0), .in3(1'b0), .in4(1'b0), .in5(1'b0), .in6(1'b0), .in7(1'b0),
    .in8(1'b0), .in10(1'b1), .in11(1'b1), .in12(1'b1), .in13(1'b1), .in14(1'b1), .in15(1'b1),
    .out(multiplexer_1_out), .sel(inst[3:0]));  // open: in9
  Multiplexer #(.select(4), .width(2)) multiplexer_2 (
    .in0(2'b10), .in1(2'b10), .in3(2'b10), .in4(2'b00), .in5(2'b01), .in6(2'b00), .in7(2'b01), .in8(2'b00),
    .in12(2'b01), .in13(2'b01), .in14(2'b01), .in15(2'b11), .out(rd_sel), .sel(inst[3:0]));  // open: in2, in9, in10, in11
  Multiplexer #(.select(4)) multiplexer_3 (
    .in0(1'b1), .in1(1'b1), .in2(1'b0), .in3(1'b1), .in4(1'b1), .in5(1'b1), .in6(1'b1), .in7(1'b1),
    .in8(1'b1), .in10(1'b1), .in11(1'b1), .in12(1'b1), .in13(1'b1), .in14(1'b0), .in15(1'b0),
    .out(alu_a_sel), .sel(inst[3:0]));  // open: in9
  Multiplexer #(.select(4)) multiplexer_4 (
    .in0(1'b0), .in1(1'b1), .in2(1'b0), .in3(1'b0), .in4(1'b1), .in5(1'b1), .in6(1'b1), .in7(1'b1),
    .in12(1'b1), .in13(1'b1), .in14(1'b1), .in15(1'b1), .out(alu_b_sel), .sel(inst[3:0]));  // open: in8, in9, in10, in11
  Multiplexer #(.select(4)) multiplexer_5 (
    .in0(1'b0), .in1(1'b0), .in2(1'b0), .in3(1'b0), .in4(1'b0), .in5(1'b0), .in6(1'b0), .in7(1'b0),
    .in8(1'b0), .in9(1'b0), .in10(1'b1), .in11(lt), .in12(lt_u), .in13(zero), .in14(1'b0), .in15(1'b0),
    .out(pc_sel), .sel(inst[3:0]));
  Multiplexer #(.select(4)) multiplexer_6 (
    .in0(1'b0), .in1(1'b0), .in2(1'b0), .in3(1'b0), .in4(1'b0), .in5(1'b0), .in6(1'b0), .in7(1'b0),
    .in8(1'b0), .in9(1'b0), .in10(1'b0), .in11(1'b0), .in12(1'b0), .in13(1'b0), .in14(1'b1), .in15(1'b1),
    .out(pc_alu_sel), .sel(inst[3:0]));
  Multiplexer multiplexer_7 (.in0(1'b0), .in1(multiplexer_8_out), .out(mem_clk), .sel(pc_clk));
  Multiplexer #(.select(4)) multiplexer_8 (
    .in0(1'b0), .in1(1'b0), .in2(1'b0), .in3(1'b0), .in4(1'b0), .in5(1'b1), .in6(1'b0), .in7(1'b1),
    .in8(1'b0), .in12(1'b0), .in13(1'b0), .in14(1'b0), .in15(1'b0), .out(multiplexer_8_out), .sel(inst[3:0]));  // open: in9, in10, in11
  Multiplexer multiplexer_9 (.in0(1'b0), .in1(multiplexer_10_out), .out(rd_clk), .sel(inst_clk));
  Multiplexer #(.select(4)) multiplexer_10 (
    .in0(1'b1), .in1(1'b1), .in2(1'b1), .in3(1'b1), .in4(1'b1), .in5(1'b0), .in6(1'b1), .in7(1'b0),
    .in8(push), .in10(1'b0), .in11(1'b0), .in12(1'b0), .in13(1'b0), .in14(1'b0), .in15(1'b1),
    .out(multiplexer_10_out), .sel(inst[3:0]));  // open: in9
  Multiplexer #(.select(4), .width(4)) multiplexer_11 (
    .in0(inst[11:8]), .in1(inst[11:8]), .in2(inst[7:4]), .in3(inst[7:4]), .in4(inst[7:4]), .in5(inst[7:4]),
    .in6(inst[7:4]), .in7(inst[7:4]), .in8(inst[7:4]), .in10(4'b0000), .in11(4'b0000), .in12(4'b0000),
    .in13(4'b0000), .in14(4'b0000), .in15(4'b1100), .out(rd), .sel(inst[3:0]));  // open: in9
  Multiplexer multiplexer_12 (.in0(multiplexer_1_out), .in1(1'b1), .out(addr_sel), .sel(inst_clk));

  // Other names for the same wires on the sheet: execute = pc_clk; fetch = inst_clk; opcode[3:0] = inst[3:0];
  //   inst1[3:0] = inst[7:4]; inst2[3:0] = inst[11:8]; inst3[3:0] = inst[15:12]
endmodule

module inst_dec (
  input  [3:0] opcode,
  output alu,
  output alu_imm,
  output li,
  output mv,
  output lb,
  output sb,
  output lw,
  output sw,
  output stack,
  output out_11,
  output out_12,
  output blt,
  output blu,
  output bnz,
  output jmp,
  output jlr
);

  Decoder #(.select(4)) decoder_1 (
    .out0(alu), .out1(alu_imm), .out2(li), .out3(mv), .out4(lb), .out5(sb), .out6(lw), .out7(sw),
    .out8(stack), .out11(blt), .out12(blu), .out13(bnz), .out14(jmp), .out15(jlr), .sel(opcode));  // open: out9, out10, en
endmodule

module control2 (
  input  clk,
  input  zero,
  input  lt,
  input  [15:0] inst,
  output addr_sel,
  output [1:0] rd_sel,
  output alu_a_sel,
  output alu_b_sel,
  output inst_in,
  output mem_in,
  output rd_in,
  output pc_in,
  output pc_sel,
  output pc_alu_sel
);

  wire button_1_out, d_ff_1_qn;
  wire [7:7] d_ff_1_q;

  D_Flip_Flop d_ff_1 (.D(d_ff_1_qn), .clk(button_1_out), .Q(d_ff_1_q[7]), .Qn(d_ff_1_qn));  // open: preset, reset
  Button button_1 (.out(button_1_out));
  ROM #(.dataWidth(11)) rom_1 (
    .addr({d_ff_1_q[7], 7'b1010000}),
    .data({pc_alu_sel, pc_sel, pc_in, rd_in, mem_in, inst_in, alu_b_sel, alu_a_sel, rd_sel, addr_sel}));

  // Notes on the sheet:
  //   contents of rom_1 (hex, n*v repeats v):
  //   21 184 122*0 18 1 18 18 184 63*0 184 31*0 184 15*0 184
endmodule

module imm_dec (
  input  [15:0] inst,
  output [15:0] imm
);

  wire b_type, decoder_1_out4, decoder_1_out5, decoder_1_out6, decoder_1_out7, decoder_1_out11,
       decoder_1_out12, decoder_1_out13, decoder_1_out14, decoder_1_out15, o_type, or_3_out, u_type;
  wire [15:0] bit_extender_1_out, bit_extender_2_out;

  Decoder #(.select(4)) decoder_1 (
    .out1(o_type), .out4(decoder_1_out4), .out5(decoder_1_out5), .out6(decoder_1_out6),
    .out7(decoder_1_out7), .out11(decoder_1_out11), .out12(decoder_1_out12), .out13(decoder_1_out13),
    .out14(decoder_1_out14), .out15(decoder_1_out15), .sel(inst[3:0]));  // open: out0, out2, out3, out8, out9, out10, en
  or or_1 (u_type, decoder_1_out4, decoder_1_out5, decoder_1_out6, decoder_1_out7);
  or or_2 (b_type, decoder_1_out11, decoder_1_out12, decoder_1_out13, decoder_1_out14, decoder_1_out15);
  or or_3 (or_3_out, o_type, u_type);
  assign bit_extender_1_out = {{12{1'b0}}, inst[15:12]};  // Bit_Extender bit_extender_1
  assign imm = or_3_out ? bit_extender_1_out : 16'bz;  // Controlled_Buffer controlled_buffer_1
  assign bit_extender_2_out = {{8{inst[15]}}, {inst[15:12], inst[7:4]}};  // Bit_Extender bit_extender_2
  assign imm = b_type ? bit_extender_2_out : 16'bz;  // Controlled_Buffer controlled_buffer_2

  // Other names for the same wires on the sheet: inst1[3:0] = inst[7:4]; inst3[3:0] = inst[15:12];
  //   inst2[3:0] = inst[11:8]
endmodule

module address_decoder (
  input  [15:0] addr,
  output microcode,
  output memory,
  output io,
  output [2:0] mem_sel,
  output bank,
  output stack
);

  wire and_1_out, multiplexer_1_out;

  nor nor_1 (microcode, addr[10], addr[11], addr[12], addr[13], addr[14], addr[15]);
  Multiplexer #(.select(4)) multiplexer_1 (
    .in0(1'b1), .in1(1'b1), .in2(1'b1), .in3(1'b1), .in4(1'b1), .in5(1'b1), .in6(1'b1), .in7(1'b1),
    .in8(1'b1), .in9(1'b1), .in10(1'b0), .in11(1'b0), .in12(1'b0), .in13(1'b0), .in14(1'b0), .in15(1'b0),
    .out(multiplexer_1_out), .sel(addr[15:12]));
  Multiplexer #(.select(4)) multiplexer_2 (
    .in0(1'b0), .in1(1'b0), .in2(1'b0), .in3(1'b0), .in4(1'b0), .in5(1'b0), .in6(1'b0), .in7(1'b0),
    .in8(1'b0), .in9(1'b0), .in10(1'b1), .in11(1'b1), .in12(1'b1), .in13(1'b1), .in14(1'b1), .in15(1'b0),
    .out(bank), .sel(addr[15:12]));
  and and_1 (and_1_out, ~microcode, multiplexer_1_out);  // AND_Gate
  Demultiplexer demultiplexer_1 (.out0(memory), .out1(io), .in(and_1_out), .sel(addr[9]));
  and and_2 (stack, addr[15], addr[14], addr[13], addr[12]);
  Priority_Encoder priority_encoder_1 (
    .in0(microcode), .in1(memory), .in2(io), .in3(bank), .in4(stack), .out(mem_sel));  // open: in5, in6, in7, en_in, gs, en_out
endmodule

module microcode (
  input  [15:0] addr,
  input  \byte ,
  output [15:0] Q
);

  wire [7:0] LSB_data, MSB_data;

  ROM #(.addrWidth(9)) LSB (.addr(addr[9:1]), .data(LSB_data));
  ROM #(.addrWidth(9)) MSB (.addr(addr[9:1]), .data(MSB_data));
  Multiplexer #(.select(2), .width(16)) multiplexer_1 (
    .in0({MSB_data, LSB_data}), .in1({16{1'b0}}), .in2({{8{1'b0}}, LSB_data}), .in3({{8{1'b0}}, MSB_data}),
    .out(Q), .sel({\byte , addr[0]}));
endmodule

module memory (
);

  RAM ram_1 ();  // open: addr, we, oe, clk, din, dout
  RAM ram_2 ();  // open: addr, we, oe, clk, din, dout
endmodule
